# Fritzing sketch fritzing-mini (saved by Fritzing 0.9.3b)

parts:
  R1 = Resistor [resistance=220 package=THT]
  LED1 = LED - 5mm [color="Red (633nm)" package="5 mm [THT]"]
  BAT1 = bat
  U1 = u  # not connected

nets:
  N1: R1.Pin_0, BAT1.connector0
  N2: R1.Pin_1, LED1.cathode
  N3: LED1.anode, BAT1.connector1
